// Logisim project mem_decoder.circ as structural Verilog: 1 circuit, main circuit main
module main (
  input  M1,
  input  M0,
  input  A15,
  input  A14,
  input  A13,
  input  A12,
  input  B3,
  input  B2,
  input  B1,
  input  B0
);

  wire and_1_out, and_2_out, and_3_out, and_4_out, and_5_out, and_6_out, and_7_out, and_8_out, and_9_out,
       and_10_out, and_11_out, and_12_out, and_13_out, and_14_out, not_1_out, not_2_out, not_3_out,
       not_4_out, not_5_out, not_6_out, not_7_out, not_8_out, or_1_out, or_2_out, or_3_out, or_4_out,
       or_5_out, or_6_out;

  not not_1 (not_1_out, M1);
  not not_2 (not_2_out, M0);
  not not_3 (not_3_out, A15);
  not not_4 (not_4_out, A14);
  not not_5 (not_5_out, A13);
  and and_1 (and_1_out, A15, not_4_out);
  and and_2 (and_2_out, A15, A14, not_5_out);
  and and_3 (and_3_out, A14, A15, not_5_out);
  not not_6 (not_6_out, and_3_out);
  or or_1 (or_1_out, M1, not_3_out, and_1_out, and_2_out);
  and and_4 (and_4_out, not_1_out, A15, A14, A13);
  and and_5 (and_5_out, not_6_out, M0);
  and and_6 (and_6_out, and_3_out, not_2_out);
  and and_7 (and_7_out, not_6_out, A15);
  and and_8 (and_8_out, and_3_out, B3);
  and and_9 (and_9_out, not_6_out, A14);
  and and_10 (and_10_out, and_3_out, B2);
  and and_11 (and_11_out, not_6_out, A13);
  and and_12 (and_12_out, and_3_out, B1);
  and and_13 (and_13_out, not_6_out, A12);
  and and_14 (and_14_out, and_3_out, B0);
  not not_7 (not_7_out, or_1_out);
  not not_8 (not_8_out, and_4_out);
  or or_2 (or_2_out, and_5_out, and_6_out);
  or or_3 (or_3_out, and_7_out, and_8_out);
  or or_4 (or_4_out, and_9_out, and_10_out);
  or or_5 (or_5_out, and_11_out, and_12_out);
  or or_6 (or_6_out, and_13_out, and_14_out);
  // Probe on not_7_out
  // Probe on not_8_out
  // Probe on or_2_out
  // Probe on or_3_out
  // Probe on or_4_out
  // Probe on or_5_out
  // Probe on or_6_out
endmodule
