// Logisim project vector_addr_selection.circ as structural Verilog: 1 circuit, main circuit main
module main (
  input  V1,
  input  V2,
  input  S2,
  input  S1,
  input  S0,
  input  VPB
);

  wire and_1_out, and_2_out, and_3_out, and_4_out, and_5_out, and_6_out, and_7_out, controlled_buffer_1_out,
       controlled_buffer_2_out, controlled_buffer_3_out, controlled_buffer_4_out, not_1_out, not_2_out,
       not_3_out, or_1_out, or_2_out, or_3_out;

  and and_1 (and_1_out, V1, V2);
  not not_1 (not_1_out, VPB);
  not not_2 (not_2_out, and_1_out);
  and and_2 (and_2_out, and_1_out, S2);
  and and_3 (and_3_out, not_2_out, 1'b1);
  and and_4 (and_4_out, and_1_out, S1);
  and and_5 (and_5_out, not_2_out, V2);
  and and_6 (and_6_out, and_1_out, S0);
  and and_7 (and_7_out, not_2_out, V1);
  not not_3 (not_3_out, and_1_out);
  or or_1 (or_1_out, and_2_out, and_3_out);
  or or_2 (or_2_out, and_4_out, and_5_out);
  or or_3 (or_3_out, and_6_out, and_7_out);
  // Probe on controlled_buffer_1_out
  assign controlled_buffer_1_out = not_1_out ? not_3_out : 1'bz;  // Controlled_Buffer controlled_buffer_1
  // Probe on controlled_buffer_2_out
  assign controlled_buffer_2_out = not_1_out ? or_1_out : 1'bz;  // Controlled_Buffer controlled_buffer_2
  // Probe on controlled_buffer_3_out
  assign controlled_buffer_3_out = not_1_out ? or_2_out : 1'bz;  // Controlled_Buffer controlled_buffer_3
  // Probe on controlled_buffer_4_out
  assign controlled_buffer_4_out = not_1_out ? or_3_out : 1'bz;  // Controlled_Buffer controlled_buffer_4
endmodule
